# Fritzing sketch UART and flyback diode (saved by Fritzing 0.9.3b)
circuit board: 2.3668cm x 1.8799cm
breadboards: 1

parts:
  R1 = Resistor [tolerance=±2% resistance=1k package=THT]
  J1 = female pin header, 2 pins [form="♀ (female)"]
  J2 = female pin header, 6 pins [form="♀ (female)"]
  R2 = Resistor [tolerance=±2% resistance=1k package=THT]
  D1 = Rectifier Diode [part_number=1N4001 package="300 mil [THT]"]
  J3 = female pin header, 2 pins [form="♀ (female)"]

nets:
  N1: R1.Pin_0, J2.pin3, J2.pin4
  N2: R1.Pin_1, J1.pin2
  N3: J1.pin1, R2.Pin_1
  N4: J2.pin1, J2.pin2, R2.Pin_0
  N5: J2.pin5, J2.pin6, D1.cathode
  N6: D1.anode, J3.pin1, J3.pin2
